// Logisim project contadores_cronometro.circ as structural Verilog: 1 circuit, main circuit main
module main (
);

  wire and_1_out, and_2_out, and_4_out, and_5_out, and_6_out, and_7_out, button_1_out, button_2_out,
       button_3_out, button_4_out, clock_1_out, clock_2_out, clock_3_out, t_ff_1_qn, t_ff_2_qn, t_ff_3_qn,
       t_ff_4_qn, undriven, undriven_2;
  wire [3:0] counter_1_q, counter_2_q, counter_3_q, counter_4_q, t_ff_1_q, t_ff_5_q;

  Clock clock_1 (.out(clock_1_out));
  Clock clock_2 (.out(clock_2_out));
  Counter #(.max('hf), .trigger("falling"), .width(4)) counter_1 (
    .count(1'b1), .Q(counter_1_q), .clk(and_2_out), .clr(and_1_out));  // open: load, D, carry, up
  and and_1 (and_1_out, counter_1_q[2], counter_1_q[1]);
  T_Flip_Flop t_ff_1 (
    .T(1'b1), .clk(clock_1_out), .Q(t_ff_1_q[0]), .Qn(t_ff_1_qn), .reset(button_1_out));  // open: preset
  Counter #(.max('hf), .trigger("falling"), .width(4)) counter_2 (
    .count(1'b1), .Q(counter_2_q), .clk(and_4_out), .clr(and_2_out));  // open: load, D, carry, up
  and and_2 (and_2_out, counter_2_q[3], counter_2_q[1]);
  // AND_Gate and_3 is placed but not wired
  Hex_Digit_Display hex_digit_display_1 (.value(t_ff_1_q));  // open: dp
  T_Flip_Flop t_ff_2 (
    .T(1'b1), .clk(t_ff_1_qn), .Q(t_ff_1_q[1]), .Qn(t_ff_2_qn), .reset(button_1_out));  // open: preset
  Hex_Digit_Display hex_digit_display_2 (.value(counter_1_q));  // open: dp
  and and_4 (and_4_out, counter_3_q[2], counter_3_q[1]);
  T_Flip_Flop t_ff_3 (
    .T(1'b1), .clk(t_ff_2_qn), .Q(t_ff_1_q[2]), .Qn(t_ff_3_qn), .reset(button_1_out));  // open: preset
  LED led_1 (.in(undriven));
  Hex_Digit_Display hex_digit_display_3 (.value(counter_2_q));  // open: dp
  LED led_2 (.in(undriven));
  Counter #(.max('h6), .trigger("falling"), .width(4)) counter_3 (
    .count(1'b1), .Q(counter_3_q), .clk(and_5_out), .clr(and_4_out));  // open: load, D, carry, up
  T_Flip_Flop t_ff_4 (
    .T(1'b1), .clk(t_ff_3_qn), .Q(t_ff_1_q[3]), .Qn(t_ff_4_qn), .reset(button_1_out));  // open: preset
  Button button_1 (.out(button_1_out));
  Hex_Digit_Display hex_digit_display_4 (.value(counter_3_q));  // open: dp
  Hex_Digit_Display hex_digit_display_5 (.value(counter_4_q));  // open: dp
  Counter #(.max('hf), .trigger("falling"), .width(4)) counter_4 (
    .count(1'b1), .Q(counter_4_q), .clk(undriven_2), .clr(and_5_out));  // open: load, D, carry, up
  Button button_2 (.out(button_2_out));
  and and_5 (and_5_out, counter_4_q[3], counter_4_q[1]);
  T_Flip_Flop t_ff_5 (.T(1'b1), .clk(clock_3_out), .Q(t_ff_5_q[0]), .reset(button_4_out));  // open: Qn, preset
  Clock clock_3 (.out(clock_3_out));
  T_Flip_Flop t_ff_6 (.T(t_ff_5_q[0]), .clk(clock_3_out), .Q(t_ff_5_q[1]), .reset(button_4_out));  // open: Qn, preset
  Hex_Digit_Display hex_digit_display_6 (.value(t_ff_5_q));  // open: dp
  and and_6 (and_6_out, t_ff_5_q[1], t_ff_5_q[0]);
  T_Flip_Flop t_ff_7 (.T(and_6_out), .clk(clock_3_out), .Q(t_ff_5_q[2]), .reset(button_4_out));  // open: Qn, preset
  Button button_3 (.out(button_3_out));
  T_Flip_Flop t_ff_8 (.T(and_7_out), .clk(clock_3_out), .Q(t_ff_5_q[3]), .reset(button_4_out));  // open: Qn, preset
  and and_7 (and_7_out, t_ff_5_q[2], and_6_out);
  Button button_4 (.out(button_4_out));

  // Notes on the sheet:
  //   ASSINCRONO
  //   SINCRONO
endmodule
