// Logisim project dadofeito.circ as structural Verilog: 1 circuit, main circuit main
module main (
  input  in_1
);

  wire and_1_out, and_2_out, and_3_out, and_4_out, and_5_out, and_6_out, and_7_out, clock_1_out, not_1_out,
       or_1_out, or_2_out, or_3_out, or_4_out, or_5_out, t_ff_1_qn, t_ff_2_qn;
  wire [2:0] t_ff_1_q;
  wire [3:0] bit_extender_1_out;

  not not_1 (not_1_out, in_1);
  Clock clock_1 (.out(clock_1_out));
  T_Flip_Flop t_ff_1 (
    .T(not_1_out), .clk(clock_1_out), .Q(t_ff_1_q[0]), .Qn(t_ff_1_qn), .reset(and_7_out));  // open: preset
  T_Flip_Flop t_ff_2 (
    .T(not_1_out), .clk(t_ff_1_qn), .Q(t_ff_1_q[1]), .Qn(t_ff_2_qn), .reset(and_7_out));  // open: preset
  T_Flip_Flop t_ff_3 (.T(not_1_out), .clk(t_ff_2_qn), .Q(t_ff_1_q[2]), .reset(and_7_out));  // open: Qn, preset
  and and_1 (and_1_out, ~t_ff_1_q[1], t_ff_1_q[0], t_ff_1_q[2]);  // AND_Gate
  and and_2 (and_2_out, ~t_ff_1_q[1], t_ff_1_q[2], ~t_ff_1_q[0]);  // AND_Gate
  and and_3 (and_3_out, t_ff_1_q[1], t_ff_1_q[0], ~t_ff_1_q[2]);  // AND_Gate
  and and_4 (and_4_out, t_ff_1_q[1], ~t_ff_1_q[0], ~t_ff_1_q[2]);  // AND_Gate
  and and_5 (and_5_out, ~t_ff_1_q[1], ~t_ff_1_q[2], t_ff_1_q[0]);  // AND_Gate
  and and_6 (and_6_out, ~t_ff_1_q[0], ~t_ff_1_q[1], ~t_ff_1_q[2]);  // AND_Gate
  and and_7 (and_7_out, t_ff_1_q[1], t_ff_1_q[2]);
  assign bit_extender_1_out = {{1{1'b0}}, t_ff_1_q};  // Bit_Extender bit_extender_1
  or or_1 (or_1_out, and_5_out, and_4_out, and_3_out, and_2_out, and_1_out);
  or or_2 (or_2_out, and_3_out, and_2_out, and_1_out);
  or or_3 (or_3_out, and_1_out, and_2_out, and_3_out, and_4_out, and_5_out);
  or or_4 (or_4_out, and_3_out, and_2_out, and_1_out);
  or or_5 (or_5_out, and_2_out, and_4_out, and_6_out);
  LED led_1 (.in(or_3_out));
  LED led_2 (.in(and_1_out));
  LED led_3 (.in(or_5_out));
  LED led_4 (.in(or_4_out));
  LED led_5 (.in(or_2_out));
  LED led_6 (.in(and_1_out));
  LED led_7 (.in(or_1_out));
  Hex_Digit_Display hex_digit_display_1 (.value(bit_extender_1_out));  // open: dp
endmodule
